# Fritzing sketch ArduinoPiBridge (saved by Fritzing 0.9.3b)
circuit board: 1.67006cm x 4.04017cm
breadboards: 1

parts:
  J9 = Raspberry Pi Header 40pin [form="♂ (male)" package=THT]
  J10 = double row male pin header, 10 pins [form="♂ (male)"]

nets:
  N1: J9.3v3, J10.pin10
  N2: J9.GND, J10.pin3
  N3: J9.GIPO15, J10.pin5
  N4: J9.GIPO14, J10.pin4
  N5: J9.5V, J10.pin1

notes:
  DigitalStables
  Wally's Saddle
  5  4  3  2  1
  Raspberry Pi
  Wally
  6  7  8  9  10
  NC  NC   NC  NC  LV
  TX  RX   GND  NC  Vcc
  RX TX   GND  NC  Vcc

custom parts:
  Raspberry Pi Header 40pin: Digital Stables Pi Arduino Bridge Pi Headers
