# Fritzing sketch Wally (saved by Fritzing 0.9.3b)
circuit board: 14.0881cm x 10.5cm
breadboards: 1

parts:
  Part1 = Logic Level Converter
  100uF1 = Capacitor Polarized [package=cpol-radial-100uf-25v]
  Power_plug1 = Power plug
  U3 = TMP36 [package=to-92]
  IC1 = DS1307 [package=THT]
  32_769 = CRYSTAL [package=tc26h]
  R3 = Resistor [tolerance=±5% resistance=220 package=THT]
  C2 = Ceramic Capacitor [capacitance=100nF package="200 mil [THT, multilayer]"]
  S1 = SWITCH-DPDT [package=ayz0202]
  R6 = Resistor [tolerance=±5% resistance=220 package=THT]
  1uF1 = Tantalum Capacitor [capacitance=1μF package="200 mil [THT, tantalum]"]
  R2 = Resistor [tolerance=±5% resistance=1M package=THT]
  R1 = Resistor [tolerance=±5% resistance=100k package=THT]
  U2 = Voltage Regulator - 5V [package="TO220 [THT]"]
  C4 = Electrolytic Capacitor [capacitance=100µF package="200 mil [THT, electrolytic]"]
  CR2033 = Battery Holders [package=battcom_20mm_pth]
  D2 = Rectifier Diode [part_number=1N4001 package="300 mil [THT]"]
  LED2 = LED - 5mm [color="Red (633nm)" package="5 mm [THT]"]
  470 = Resistor [tolerance=±5% resistance=470 package=THT]
  10k1 = Resistor [tolerance=±5% resistance=10k package=THT]
  1k1 = Resistor [tolerance=±5% resistance=1k package=THT]
  sdCard2 = my_sdCard
  Q2 = NPN-Transistor [package="TO92 [THT]"]
  SCL_SDA_Gnd_Vcc = screw terminal, 4 pins
  SCL_SDA_Gnd_VcC = screw terminal, 4 pins
  Squix1 = OLED 0.96" 128x64 I2C SSD1306
  R7 = Resistor [tolerance=±5% resistance=47k package=THT]
  R8 = Resistor [tolerance=±5% resistance=22k package=THT]
  R9 = Resistor [tolerance=±5% resistance=10k package=THT]
  S4 = Pushbutton [package="[THT]"]
  S3 = Pushbutton [package="[THT]"]
  S5 = Pushbutton [package="[THT]"]
  D2_+_- = screw terminal, 3 pins
  D3_+_- = screw terminal, 3 pins
  R10 = Resistor [tolerance=±5% resistance=220k package=THT]
  R11 = Resistor [tolerance=±5% resistance=220k package=THT]
  Part4 = Arduino Pro Mini (5V)
  J1 = shrouded pin header, 10 pins [form="♂ (shrouded male)"]
  U6 = XBEE-1 [package=xbee-silk]
  D10_D11_+_-1 = screw terminal, 3 pins  # not connected
  J2 = Screw terminal - 2 pins [package=THT]
  J3 = Screw terminal - 2 pins [package=THT]
  J4 = Screw terminal - 2 pins [package=THT]
  R12 = Resistor [tolerance=±5% resistance=100k package=THT]
  R13 = Resistor [tolerance=±5% resistance=4.7k package=THT]
  R14 = Resistor [tolerance=±5% resistance=3.3k package=THT]
  R15 = Resistor [tolerance=±5% resistance=2.2k package=THT]
  A7_+_- = screw terminal, 3 pins
  A6_+_- = screw terminal, 3 pins
  D8_+_- = screw terminal, 3 pins

nets:
  N1: Part1.TX2_LV, J1.pin4
  N2: Part1.RX2_LV, J1.pin5
  GND: Part1.GND, 100uF1.-, Power_plug1.GND, U3.GND, S1.2, 1uF1.-, R1.Pin_1, U2.GND, 10k1.Pin_1, sdCard2.GND, Q2.E, SCL_SDA_Gnd_Vcc.pin2, SCL_SDA_Gnd_VcC.pin2, Squix1.GND, D2_+_-.pin1, D3_+_-.pin1, Part4.GND, J1.pin3, U6.GND, R12.Pin_1, A7_+_-.pin1, A6_+_-.pin1, D8_+_-.pin1
  N3: Part1.LV, J1.pin10, U6.VDD
  N4: Part1.RX_LV, U6.DIN
  N5: Part1.TX_LV, U6.DOUT
  N6: Part1.TX_HV, Part4.D5
  N7: Part1.RX_HV, Part4.D6
  VCC: Part1.HV, U3.VCC, 1uF1.+, U2.output_voltage, D2.cathode, 470.Pin_0, sdCard2.VCC, SCL_SDA_Gnd_Vcc.pin1, SCL_SDA_Gnd_VcC.pin1, Squix1.VCC, R7.Pin_0, R7.Pin_1, R8.Pin_0, R8.Pin_1, R9.Pin_0, R9.Pin_1, S4.Pin_1, S4.Pin_2, S3.Pin_1, S3.Pin_2, S5.Pin_1, S5.Pin_2, D2_+_-.pin2, D2_+_-.pin3, D3_+_-.pin2, D3_+_-.pin3, R10.Pin_0, R11.Pin_0, Part4.VCC, J1.pin1, R13.Pin_1, R14.Pin_1, R15.Pin_1, A7_+_-.pin2, A6_+_-.pin2, D8_+_-.pin2
  N8: Part1.RX2_HV, Part4.TXO
  N9: Part1.TX2_HV, Part4.RXI
  N10: 100uF1.+, Power_plug1.VCC, R2.Pin_0, U2.input_voltage
  N11: U3.VOUT, Part4.A1
  N12: IC1.X1_-_Crystal, 32_769.2
  N13: IC1.X2_-_Crystal, 32_769.1
  N14: IC1.Vbat_-_Backup_Supply, CR2033.+
  N15: IC1.0V, C2.0, CR2033.-
  N16: IC1.SDA_-_I2C_Data, R6.Pin_1, SCL_SDA_Gnd_Vcc.pin3, SCL_SDA_Gnd_VcC.pin3, Squix1.SCA, Part4.A4
  N17: IC1.SCL_-_I2C_Clock, R3.Pin_1, SCL_SDA_Gnd_Vcc.pin4, SCL_SDA_Gnd_VcC.pin4, Squix1.SCL, Part4.A5
  N18: IC1.+V, R3.Pin_0, C2.1, R6.Pin_0
  N19: S1.1, C4.-, Part4.A3
  N20: R2.Pin_1, R1.Pin_0, Part4.A2
  N21: C4.+, Part4.RESET
  N22: D2.anode, LED2.cathode, Q2.C
  N23: LED2.anode, 470.Pin_1
  N24: 10k1.Pin_0, 1k1.Pin_0, Q2.B
  N25: 1k1.Pin_1, Part4.D4
  N26: sdCard2.MISO, Part4.MISO
  N27: sdCard2.MOSI, Part4.MOSI
  N28: sdCard2.SCK, Part4.SCK
  N29: sdCard2.CS, Part4.D10
  N30: S4.Pin_3, S4.Pin_4, S3.Pin_3, S3.Pin_4, S5.Pin_3, S5.Pin_4, Part4.A0, J2.pin1, J3.pin1, J4.pin1, R12.Pin_0
  N31: R10.Pin_1, Part4.D2
  N32: R11.Pin_1, Part4.D3
  N33: Part4.A6, A7_+_-.pin3
  N34: Part4.A7, A6_+_-.pin3
  N35: Part4.D8, D8_+_-.pin3
  N36: J2.pin2, R13.Pin_0
  N37: J3.pin2, R14.Pin_0
  N38: J4.pin2, R15.Pin_0

notes:
  DigitalStables
  Wally
  V 1.0 Revision d
  Arduino Pro Mini 5V 16Mhz
  A0 - Buttons
  A1 - Temperature
  A2 - Battery Voltage
  A3 - Lock Capacitor Voltage
  A4- I2C Data
  A5 - I2C Clock
  D4 - Relay
  D5 XBee RX (Connected to Pin 2 DOUT Xbee)
  D6 XBee TX (Connected to Pin 3 DIn Xbee)
  D7 - 12V Regulated
  D9 5V Raspberry Pi power line
  D10, D11, D12, D13 - SD Card
  Available ports
  A6
  A7
  D2
  D3
  D8
  Ari Fainchtein
  0406 759 601
  ari@digitalstables.com

custom parts:
  my_sdCard: micro sdCard Adapter with 90º pin header. Use a filtering Capacitor between CS and GND if needed. PCB View Pinouts are Reversed for laying parallel on PCB using a 90º pin header.
